// Logisim project ALU.circ as structural Verilog: 2 circuits, main circuit ALU
module ALU (
  input  [31:0] A,
  input  [31:0] B,
  input  [4:0] Shift,
  input  CarryIn,
  input  [3:0] Codop,
  output [31:0] S,
  output [3:0] Flags
);

  wire adder_1_cout, adder_2_cout, and_3_out, and_4_out, bitselector_1_out, bitselector_2_out,
       bitselector_3_out, bitselector_4_out, bitselector_5_out, bitselector_6_out, bitselector_7_out,
       comparator_1_eq, comparator_2_eq, comparator_3_eq, comparator_4_eq, not_1_out, not_3_out, not_4_out,
       not_5_out, not_6_out, resultatperdu_1_perdu, subtractor_1_bout, subtractor_2_bout;
  wire [31:0] adder_1_out, adder_2_out, and_1_out, and_2_out, multiplexer_1_out, multiplexer_2_out,
       multiplexer_3_out, multiplier_1_cout, multiplier_1_out, negator_1_out, not_2_out, or_1_out,
       shifter_1_out, shifter_2_out, shifter_3_out, shifter_4_out, subtractor_1_out, subtractor_2_out,
       xor_1_out;

  not not_1 (not_1_out, CarryIn);
  assign and_1_out = A & B;  // AND_Gate and_1, 32 bits wide
  assign xor_1_out = A ^ B;  // XOR_Gate xor_1, 32 bits wide
  Shifter #(.width(32)) shifter_1 (.in(B), .\dist (Shift), .out(shifter_1_out));
  Shifter #(.shift("lr"), .width(32)) shifter_2 (.in(B), .\dist (Shift), .out(shifter_2_out));
  Shifter #(.shift("ar"), .width(32)) shifter_3 (.in(B), .\dist (Shift), .out(shifter_3_out));
  Adder #(.width(32)) adder_1 (.a(A), .b(B), .out(adder_1_out), .cin(CarryIn), .cout(adder_1_cout));
  Subtractor #(.width(32)) subtractor_1 (
    .a(B), .b(A), .out(subtractor_1_out), .bin(not_1_out), .bout(subtractor_1_bout));
  Shifter #(.shift("rr"), .width(32)) shifter_4 (.in(B), .\dist (Shift), .out(shifter_4_out));
  Negator #(.width(32)) negator_1 (.in(A), .out(negator_1_out));
  Subtractor #(.width(32)) subtractor_2 (.a(B), .b(A), .out(subtractor_2_out), .bout(subtractor_2_bout));  // open: bin
  Adder #(.width(32)) adder_2 (.a(A), .b(B), .out(adder_2_out), .cout(adder_2_cout));  // open: cin
  assign or_1_out = A | B;  // OR_Gate or_1, 32 bits wide
  Multiplier #(.width(32)) multiplier_1 (.a(A), .b(B), .out(multiplier_1_out), .cout(multiplier_1_cout));  // open: cin
  assign and_2_out = ~A & B;  // AND_Gate and_2, 32 bits wide
  assign not_2_out = ~B;  // NOT_Gate not_2, 32 bits wide
  not not_3 (not_3_out, subtractor_1_bout);
  not not_4 (not_4_out, subtractor_2_bout);
  Multiplexer #(.enable("false"), .select(4), .width(32)) multiplexer_1 (
    .in0({32{1'b0}}), .in1({32{1'b0}}), .in2({32{1'b0}}), .in3({32{1'b0}}), .in4({32{1'b0}}),
    .in5(adder_1_out), .in6({32{1'b0}}), .in7({32{1'b0}}), .in8({32{1'b0}}), .in9({32{1'b0}}),
    .in10({32{1'b0}}), .in11(adder_2_out), .in12({32{1'b0}}), .in13({32{1'b0}}), .in14({32{1'b0}}),
    .in15({32{1'b0}}), .out(multiplexer_1_out), .sel(Codop));
  Multiplexer #(.enable("false"), .select(4), .width(32)) multiplexer_2 (
    .in0({32{1'b0}}), .in1({32{1'b0}}), .in2({32{1'b0}}), .in3({32{1'b0}}), .in4({32{1'b0}}),
    .in5({32{1'b0}}), .in6(subtractor_1_out), .in7({32{1'b0}}), .in8({32{1'b0}}), .in9({32{1'b0}}),
    .in10(subtractor_2_out), .in11({32{1'b0}}), .in12({32{1'b0}}), .in13({32{1'b0}}), .in14({32{1'b0}}),
    .in15({32{1'b0}}), .out(multiplexer_2_out), .sel(Codop));
  BitSelector #(.width(32)) bitselector_1 (.in(multiplier_1_cout), .out(bitselector_1_out), .sel({5{1'b0}}));
  BitSelector #(.width(32)) bitselector_2 (.in(A), .out(bitselector_2_out), .sel({5{1'b1}}));
  BitSelector #(.width(32)) bitselector_3 (.in(B), .out(bitselector_3_out), .sel({5{1'b1}}));
  BitSelector #(.width(32)) bitselector_4 (.in(multiplexer_1_out), .out(bitselector_4_out), .sel({5{1'b1}}));
  BitSelector #(.width(32)) bitselector_5 (.in(multiplexer_2_out), .out(bitselector_5_out), .sel({5{1'b1}}));
  BitSelector #(.width(32)) bitselector_6 (.in(A), .out(bitselector_6_out), .sel({5{1'b1}}));
  BitSelector #(.width(32)) bitselector_7 (.in(B), .out(bitselector_7_out), .sel({5{1'b1}}));
  Multiplexer #(.enable("false"), .select(4), .width(32)) multiplexer_3 (
    .in0(and_1_out), .in1(xor_1_out), .in2(shifter_1_out), .in3(shifter_2_out), .in4(shifter_3_out),
    .in5(adder_1_out), .in6(subtractor_1_out), .in7(shifter_4_out), .in8(and_1_out), .in9(negator_1_out),
    .in10(subtractor_2_out), .in11(adder_2_out), .in12(or_1_out), .in13(multiplier_1_out), .in14(and_2_out),
    .in15(not_2_out), .out(multiplexer_3_out), .sel(Codop));
  Multiplexer #(.enable("false"), .select(4)) multiplexer_4 (
    .in0(1'b0), .in1(1'b0), .in2(1'b0), .in3(1'b0), .in4(1'b0), .in5(adder_1_cout), .in6(not_3_out),
    .in7(1'b0), .in8(1'b0), .in9(1'b0), .in10(not_4_out), .in11(adder_2_cout), .in12(1'b0),
    .in13(bitselector_1_out), .in14(1'b0), .in15(1'b0), .out(Flags[1]), .sel(Codop));
  Comparator #(.width(1)) comparator_1 (
    .a(bitselector_2_out), .b(bitselector_3_out), .eq(comparator_1_eq));  // open: gt, lt
  Comparator #(.width(1)) comparator_2 (
    .a(bitselector_3_out), .b(bitselector_4_out), .eq(comparator_2_eq));  // open: gt, lt
  Comparator #(.width(1)) comparator_3 (
    .a(bitselector_5_out), .b(bitselector_6_out), .eq(comparator_3_eq));  // open: gt, lt
  Comparator #(.width(1)) comparator_4 (
    .a(bitselector_6_out), .b(bitselector_7_out), .eq(comparator_4_eq));  // open: gt, lt
  Comparator #(.width(32)) comparator_5 (
    .a(multiplexer_3_out), .b({32{1'b0}}), .eq(Flags[2]), .lt(Flags[3]));  // open: gt
  not not_5 (not_5_out, comparator_2_eq);
  not not_6 (not_6_out, comparator_4_eq);
  Multiplexer #(.enable("false"), .select(4)) multiplexer_5 (
    .in0(1'b0), .in1(1'b0), .in2(1'b0), .in3(1'b0), .in4(1'b0), .in5(and_3_out), .in6(and_4_out), .in7(1'b0),
    .in8(1'b0), .in9(1'b0), .in10(and_4_out), .in11(and_3_out), .in12(1'b0), .in13(1'b0), .in14(1'b0),
    .in15(1'b0), .out(Flags[0]), .sel(Codop));
  and and_3 (and_3_out, comparator_1_eq, not_5_out);
  Multiplexer #(.enable("false"), .width(32)) multiplexer_6 (
    .in0(multiplexer_3_out), .in1(B), .out(S), .sel(resultatperdu_1_perdu));
  and and_4 (and_4_out, comparator_3_eq, not_6_out);
  ResultatPerdu resultatperdu_1 (
    .Bit3(Codop[3]), .Bit2(Codop[2]), .Bit1(Codop[1]), .Bit0(Codop[0]), .Perdu(resultatperdu_1_perdu));

  // Notes on the sheet:
  //   Note: for ROR, C = N
  //   Note 2: assume that shift > 0 for LSL and LSR
endmodule

module ResultatPerdu (
  input  Bit3,
  input  Bit2,
  input  Bit1,
  input  Bit0,
  output Perdu
);

  wire and_1_out, and_2_out, not_1_out, not_2_out;

  not not_1 (not_1_out, Bit2);
  not not_2 (not_2_out, Bit0);
  and and_1 (and_1_out, Bit3, not_1_out, not_2_out);
  and and_2 (and_2_out, Bit3, not_1_out, Bit1);
  or or_1 (Perdu, and_1_out, and_2_out);
endmodule
