// Logisim project BancDeRegistres.circ as structural Verilog: 1 circuit, main circuit BancRegistre
module BancRegistre (
  input  [31:0] DataIn,
  input  [2:0] RegDest,
  input  Clk,
  input  Reset,
  input  [2:0] RegA,
  input  [2:0] RegB,
  output [31:0] AOut,
  output [31:0] BOut,
  output [31:0] R0,
  output [31:0] R1,
  output [31:0] R2,
  output [31:0] R3,
  output [31:0] R4,
  output [31:0] R5,
  output [31:0] R6,
  output [31:0] R7
);

  wire decoder_1_out0, decoder_1_out1, decoder_1_out2, decoder_1_out3, decoder_1_out4, decoder_1_out5,
       decoder_1_out6, decoder_1_out7, undriven_2;
  wire [31:0] undriven;

  Decoder #(.enable("false"), .select(3)) decoder_1 (
    .out0(decoder_1_out0), .out1(decoder_1_out1), .out2(decoder_1_out2), .out3(decoder_1_out3),
    .out4(decoder_1_out4), .out5(decoder_1_out5), .out6(decoder_1_out6), .out7(decoder_1_out7), .sel(RegDest));
  Register #(.width(32)) register_1 (.D(undriven), .en(decoder_1_out0), .clk(Clk), .Q(R0), .clr(undriven_2));
  Register #(.width(32)) register_2 (.D(undriven), .en(decoder_1_out1), .clk(Clk), .Q(R1), .clr(undriven_2));
  Register #(.width(32)) register_3 (.D(undriven), .en(decoder_1_out2), .clk(Clk), .Q(R2), .clr(undriven_2));
  Register #(.width(32)) register_4 (.D(undriven), .en(decoder_1_out3), .clk(Clk), .Q(R3), .clr(undriven_2));
  Register #(.width(32)) register_5 (.D(undriven), .en(decoder_1_out4), .clk(Clk), .Q(R4), .clr(undriven_2));
  Register #(.width(32)) register_6 (.D(undriven), .en(decoder_1_out5), .clk(Clk), .Q(R5), .clr(undriven_2));
  Register #(.width(32)) register_7 (.D(undriven), .en(decoder_1_out6), .clk(Clk), .Q(R6), .clr(undriven_2));
  Register #(.width(32)) register_8 (.D(undriven), .en(decoder_1_out7), .clk(Clk), .Q(R7), .clr(undriven_2));
  Multiplexer #(.enable("false"), .select(3), .width(32)) multiplexer_1 (
    .in0(R0), .in1(R1), .in2(R2), .in3(R3), .in4(R4), .in5(R5), .in6(R6), .in7(R7), .out(AOut), .sel(RegA));
  Multiplexer #(.enable("false"), .select(3), .width(32)) multiplexer_2 (
    .in0(R0), .in1(R1), .in2(R2), .in3(R3), .in4(R4), .in5(R5), .in6(R6), .in7(R7), .out(BOut), .sel(RegB));
endmodule
