// Logisim project Ctl_Conditional.circ as structural Verilog: 1 circuit, main circuit Conditional
module Conditional (
  input  Enable,
  input  [15:0] Instruction,
  input  Z,
  input  C,
  input  N,
  input  V,
  output [10:0] Offset,
  output Verified
);

  wire and_1_out, and_2_out, comparator_1_eq, comparator_1_lt, comparator_2_eq, comparator_2_lt,
       comparator_3_eq, comparator_3_lt, comparator_4_eq, comparator_4_lt, comparator_5_eq,
       multiplexer_2_out, not_1_out, not_2_out, not_3_out, or_1_out, or_2_out, or_3_out;
  wire [10:0] bit_extender_1_out, multiplexer_1_out;

  Comparator #(.mode("unsigned"), .width(1)) comparator_1 (
    .a(Z), .b(1'b1), .eq(comparator_1_eq), .lt(comparator_1_lt));  // open: gt
  Comparator #(.mode("unsigned"), .width(1)) comparator_2 (
    .a(C), .b(1'b1), .eq(comparator_2_eq), .lt(comparator_2_lt));  // open: gt
  Comparator #(.mode("unsigned"), .width(1)) comparator_3 (
    .a(N), .b(1'b1), .eq(comparator_3_eq), .lt(comparator_3_lt));  // open: gt
  Comparator #(.mode("unsigned"), .width(1)) comparator_4 (
    .a(V), .b(1'b1), .eq(comparator_4_eq), .lt(comparator_4_lt));  // open: gt
  Comparator #(.mode("unsigned"), .width(1)) comparator_5 (.a(N), .b(V), .eq(comparator_5_eq));  // open: gt, lt
  and and_1 (and_1_out, comparator_1_lt, comparator_2_eq);
  assign bit_extender_1_out = {{3{Instruction[7]}}, Instruction[7:0]};  // Bit_Extender bit_extender_1
  or or_1 (or_1_out, comparator_1_eq, comparator_2_lt);
  and and_2 (and_2_out, comparator_1_lt, comparator_5_eq);
  not not_1 (not_1_out, comparator_5_eq);
  or or_2 (or_2_out, comparator_1_eq, not_1_out);
  not not_2 (not_2_out, Instruction[13]);
  Multiplexer #(.enable("false"), .width(11)) multiplexer_1 (
    .in0(Instruction[10:0]), .in1(bit_extender_1_out), .out(multiplexer_1_out), .sel(not_2_out));
  not not_3 (not_3_out, comparator_5_eq);
  or or_3 (or_3_out, Instruction[13], multiplexer_2_out);
  Multiplexer #(.select(4)) multiplexer_2 (
    .in0(comparator_1_eq), .in1(comparator_1_lt), .in2(comparator_2_eq), .in3(comparator_2_lt),
    .in4(comparator_3_eq), .in5(comparator_3_lt), .in6(comparator_4_eq), .in7(comparator_4_lt),
    .in8(and_1_out), .in9(or_1_out), .in10(comparator_5_eq), .in11(not_3_out), .in12(and_2_out),
    .in13(or_2_out), .in14(1'b1), .in15(1'b0), .out(multiplexer_2_out), .sel(Instruction[11:8]), .en(Enable));
  Multiplexer #(.enable("false"), .width(11)) multiplexer_3 (
    .in0({11{1'b0}}), .in1(multiplexer_1_out), .out(Offset), .sel(Enable));
  and and_3 (Verified, Enable, or_3_out);
endmodule
