// Logisim project Ctl_Load_Store.circ as structural Verilog: 1 circuit, main circuit Load_Store
module Load_Store (
  input  Clk,
  input  Reset,
  input  Enable,
  input  [31:0] Stack_Pointer,
  input  [15:0] Instruction,
  output PC_Hold,
  output Load,
  output Store,
  output [2:0] Rmd,
  output [31:0] RAM_Addr
);

  wire and_1_out, bitselector_2_out, comparator_1_eq, comparator_1_gt, not_1_out;
  wire [2:0] bitselector_4_out;
  wire [7:0] bitselector_1_out, bitselector_3_out;
  wire [31:0] adder_1_out, bit_extender_1_out;

  and and_1 (and_1_out, not_1_out, comparator_1_gt);
  D_Flip_Flop d_ff_1 (.D(and_1_out), .clk(Clk), .Q(PC_Hold), .reset(Reset));  // open: Qn, preset
  BitSelector #(.group(8), .width(16)) bitselector_1 (.in(Instruction), .out(bitselector_1_out), .sel(1'b0));
  BitSelector #(.width(16)) bitselector_2 (.in(Instruction), .out(bitselector_2_out), .sel(4'b1011));
  BitSelector #(.group(8), .width(16)) bitselector_3 (.in(Instruction), .out(bitselector_3_out), .sel(1'b1));
  assign bit_extender_1_out = {{24{1'b0}}, bitselector_1_out};  // Bit_Extender bit_extender_1
  Comparator #(.width(1)) comparator_1 (
    .a(bitselector_2_out), .b(1'b0), .gt(comparator_1_gt), .eq(comparator_1_eq));  // open: lt
  BitSelector #(.group(3)) bitselector_4 (.in(bitselector_3_out), .out(bitselector_4_out), .sel(2'b00));
  not not_1 (not_1_out, PC_Hold);
  Adder #(.width(32)) adder_1 (.a(Stack_Pointer), .b(bit_extender_1_out), .out(adder_1_out));  // open: cin, cout
  Multiplexer #(.enable("false"), .width(32)) multiplexer_1 (
    .in0({32{1'b0}}), .in1(adder_1_out), .out(RAM_Addr), .sel(Enable));
  Multiplexer #(.enable("false")) multiplexer_2 (.in0(1'b0), .in1(comparator_1_gt), .out(Load), .sel(Enable));
  Multiplexer #(.enable("false")) multiplexer_3 (.in0(1'b0), .in1(comparator_1_eq), .out(Store), .sel(Enable));
  Multiplexer #(.enable("false"), .width(3)) multiplexer_4 (
    .in0(3'b000), .in1(bitselector_4_out), .out(Rmd), .sel(Enable));

  // Notes on the sheet:
  //   Instruction: pull=down
  //   Delay load and hold PC for 1 cycle for the RAM to send out requested data 
endmodule
