// Logisim project Ctl_Shift_Add_Sub_Mov.circ as structural Verilog
module Shift_Add_Sub_Mov (
  input  Enable,
  input  [15:0] Instruction,
  output [3:0] Flags_Update_Mask,
  output Carry,
  output Imm32_Enable,
  output [2:0] Rm,
  output [2:0] Rn,
  output [2:0] Rd,
  output [4:0] Imm5,
  output [31:0] Imm32,
  output [3:0] ALU_Opcode
);

  wire carry_table_1_carry, imm32_table_1_imm32;
  wire [2:0] bitselector_4_out, bitselector_6_out, bitselector_7_out, bitselector_8_out, bitselector_10_out,
       multiplexer_1_out, multiplexer_2_out;
  wire [3:0] flags_table_1_flags, table_verite_1_codop;
  wire [4:0] bitselector_3_out, bitselector_11_out;
  wire [7:0] bitselector_9_out;
  wire [8:0] bitselector_1_out;
  wire [10:0] bitselector_2_out, bitselector_5_out;

  BitSelector #(.group(9), .width(16)) bitselector_1 (.in(Instruction), .out(bitselector_1_out), .sel(1'b1));
  BitSelector #(.group(11), .width(16)) bitselector_2 (.in(Instruction), .out(bitselector_2_out), .sel(1'b0));
  BitSelector #(.group(5), .width(9)) bitselector_3 (.in(bitselector_1_out), .out(bitselector_3_out), .sel(1'b0));
  BitSelector #(.group(3), .width(16)) bitselector_4 (.in(Instruction), .out(bitselector_4_out), .sel(3'b010));
  BitSelector #(.group(11), .width(16)) bitselector_5 (.in(Instruction), .out(bitselector_5_out), .sel(1'b1));
  BitSelector #(.group(3), .width(11)) bitselector_6 (.in(bitselector_5_out), .out(bitselector_6_out), .sel(2'b11));
  BitSelector #(.group(3), .width(16)) bitselector_7 (.in(Instruction), .out(bitselector_7_out), .sel(3'b001));
  BitSelector #(.group(3), .width(16)) bitselector_8 (.in(Instruction), .out(bitselector_8_out), .sel(3'b000));
  BitSelector #(.group(8), .width(16)) bitselector_9 (.in(Instruction), .out(bitselector_9_out), .sel(1'b1));
  BitSelector #(.group(3)) bitselector_10 (.in(bitselector_9_out), .out(bitselector_10_out), .sel(2'b00));
  BitSelector #(.group(5), .width(11)) bitselector_11 (.in(bitselector_2_out), .out(bitselector_11_out), .sel(2'b10));
  Multiplexer #(.enable("false"), .width(3)) multiplexer_1 (
    .in0(bitselector_4_out), .in1(bitselector_6_out), .out(multiplexer_1_out), .sel(Enable));
  Multiplexer #(.enable("false"), .width(3)) multiplexer_2 (
    .in0(bitselector_8_out), .in1(bitselector_10_out), .out(multiplexer_2_out), .sel(Enable));
  flags_table flags_table_1 (.codop(bitselector_3_out), .flags(flags_table_1_flags));
  carry_table carry_table_1 (.codop(bitselector_3_out), .carry(carry_table_1_carry));
  imm32_table imm32_table_1 (.opcode(bitselector_3_out), .imm32(imm32_table_1_imm32));
  table_verite table_verite_1 (.opcode(bitselector_3_out), .codop(table_verite_1_codop));
  Multiplexer #(.enable("false"), .width(4)) multiplexer_3 (
    .in0(4'b0000), .in1(flags_table_1_flags), .out(Flags_Update_Mask), .sel(Enable));
  Multiplexer #(.enable("false")) multiplexer_4 (.in0(1'b0), .in1(carry_table_1_carry), .out(Carry), .sel(Enable));
  Multiplexer #(.enable("false")) multiplexer_5 (
    .in0(1'b0), .in1(imm32_table_1_imm32), .out(Imm32_Enable), .sel(Enable));
  Multiplexer #(.enable("false"), .width(3)) multiplexer_6 (
    .in0(3'b000), .in1(multiplexer_1_out), .out(Rm), .sel(Enable));
  Multiplexer #(.enable("false"), .width(3)) multiplexer_7 (
    .in0(3'b000), .in1(bitselector_7_out), .out(Rn), .sel(Enable));
  Multiplexer #(.enable("false"), .width(3)) multiplexer_8 (
    .in0(3'b000), .in1(multiplexer_2_out), .out(Rd), .sel(Enable));
  Multiplexer #(.enable("false"), .width(5)) multiplexer_9 (
    .in0({5{1'b0}}), .in1(bitselector_11_out), .out(Imm5), .sel(Enable));
  Multiplexer #(.enable("false"), .width(32)) multiplexer_10 (
    .in0({32{1'b0}}), .in1({32{1'b0}}), .out(Imm32), .sel(Enable));
  Multiplexer #(.enable("false"), .width(4)) multiplexer_11 (
    .in0(4'b0000), .in1(table_verite_1_codop), .out(ALU_Opcode), .sel(Enable));

  // Notes on the sheet:
  //   Note: ALU uses Rn register for shifts. Use Rn instead of Rm for shifts (immediate) here too
  //   Note 2: MOV uses RSB ALU opcode with Imm8 reversed so that it is copied to output register
  //   Note 3: Imm32_Enable forces the use of the immediate for Rm register
  //   Pull output low on Enable = 0
  //   Enable carry for SUB since it is reversed in ALU
  //   ALU will use Imm32 instead of Rm
  //   only ADD and SUB use Rm
endmodule

module flags_table (
  input  [4:0] codop,
  output [3:0] flags
);

  wire and_1_out, and_2_out, and_3_out, not_1_out;

  not not_1 (not_1_out, codop[4]);
  or or_1 (flags[1], not_1_out, codop[2], codop[3]);
  and and_1 (and_1_out, codop[3], codop[2]);
  and and_2 (and_2_out, codop[4], codop[2]);
  and and_3 (and_3_out, codop[4], codop[3]);
  or or_2 (flags[0], and_1_out, and_2_out, and_3_out);

  assign flags[3:2] = 2'b11;
endmodule

module carry_table (
  input  [4:0] codop,
  output carry
);

  wire and_1_out, not_1_out, not_2_out, not_3_out;

  not not_1 (not_1_out, codop[3]);
  not not_2 (not_2_out, codop[2]);
  not not_3 (not_3_out, codop[1]);
  and and_1 (and_1_out, not_1_out, not_3_out);
  or or_1 (carry, and_1_out, not_2_out, codop[0], codop[4]);
endmodule

module imm32_table (
  input  [4:0] opcode,
  output imm32
);

  wire not_1_out;

  not not_1 (not_1_out, opcode[4]);
  and and_1 (imm32, not_1_out, opcode[2]);
endmodule

module table_verite (
  input  [4:0] opcode,
  output [3:0] codop
);

  wire and_1_out, and_2_out, and_3_out, and_4_out, and_5_out, and_6_out, and_7_out, and_8_out, and_9_out,
       not_1_out, not_2_out, not_3_out, not_4_out, not_5_out;

  not not_1 (not_1_out, opcode[4]);
  not not_2 (not_2_out, opcode[3]);
  not not_3 (not_3_out, opcode[2]);
  not not_4 (not_4_out, opcode[1]);
  not not_5 (not_5_out, opcode[0]);
  and and_1 (and_1_out, opcode[3], opcode[2]);
  or or_1 (codop[2], and_1_out, opcode[4]);
  and and_2 (and_2_out, not_1_out, not_2_out, opcode[2]);
  and and_3 (and_3_out, not_1_out, opcode[3], not_3_out);
  and and_4 (and_4_out, opcode[3], not_3_out, opcode[1], opcode[0]);
  and and_5 (and_5_out, opcode[4], opcode[3], opcode[2]);
  and and_6 (and_6_out, not_1_out, not_3_out);
  and and_7 (and_7_out, opcode[3], not_3_out, not_4_out);
  and and_8 (and_8_out, opcode[3], not_3_out, not_5_out);
  and and_9 (and_9_out, opcode[4], not_2_out, opcode[2]);
  or or_2 (codop[1], and_2_out, and_3_out, and_4_out, and_5_out);
  or or_3 (codop[0], and_6_out, and_7_out, and_8_out, and_9_out);

  assign codop[3] = 1'b0;
endmodule
